// Logisim project labac.circ as structural Verilog: 1 circuit, main circuit main
module main (
  input  in_1,
  input  in_2,
  input  in_3,
  input  in_4,
  input  in_5,
  input  in_6,
  input  in_7,
  input  in_8,
  input  in_9,
  input  in_10,
  output out_11,
  output out_12,
  output out_13,
  output out_14
);

  wire button_1_out, multiplexer_1_out, not_1_out;

  Button button_1 (.out(button_1_out));
  Multiplexer multiplexer_1 (.in0(in_1), .in1(in_3), .out(multiplexer_1_out), .sel(in_4), .en(in_5));
  LED led_1 (.in(button_1_out));
  LED led_2 (.in(not_1_out));
  not not_1 (not_1_out, button_1_out);
  LED led_3 (.in(multiplexer_1_out));
  xnor xnor_1 (out_14, in_9, in_10);
  or or_1 (out_13, in_7, in_8);
  D_Flip_Flop d_ff_1 (.clk(in_2), .D(in_6), .Q(out_11), .Qn(out_12));  // open: preset, en, reset
endmodule
