// Logisim project medium.circ as structural Verilog: 20 circuits, main circuit 1m
module _1m (
  input  in_1,
  input  in_2
);

  wire xnor_1_out;

  xnor xnor_1 (xnor_1_out, in_1, in_2);
  LED led_1 (.in(xnor_1_out));
endmodule

module _2m (
  input  in_1,
  input  in_2
);

  wire or_1_out;

  or or_1 (or_1_out, in_1, in_2);
  LED led_1 (.in(or_1_out));
endmodule

module _3m (
  input  in_1,
  input  in_2
);

  wire xor_1_out;

  xor xor_1 (xor_1_out, in_1, in_2);
  LED led_1 (.in(xor_1_out));
endmodule

module _4m (
  input  in_1,
  input  in_2
);

  wire xor_1_out;

  xor xor_1 (xor_1_out, in_1, in_2);
  LED led_1 (.in(xor_1_out));
endmodule

module _5m (
  input  in_1,
  input  in_2
);

  wire xor_1_out;

  xor xor_1 (xor_1_out, in_1, in_2);
  LED led_1 (.in(xor_1_out));
endmodule

module _6m (
  input  in_1,
  input  in_2
);

  wire and_1_out;

  and and_1 (and_1_out, ~in_1, ~in_2);  // AND_Gate
  LED led_1 (.in(and_1_out));
endmodule

module _7m (
  input  in_1,
  input  in_2
);

  wire and_1_out;

  and and_1 (and_1_out, in_1, in_2);
  LED led_1 (.in(and_1_out));
endmodule

module _8m (
  input  in_1
);

  wire not_1_out, xor_1_out;

  not not_1 (not_1_out, in_1);
  xor xor_1 (xor_1_out, not_1_out, in_1);
  LED led_1 (.in(xor_1_out));
endmodule

module _9m (
  input  in_1
);

  wire nor_1_out;

  nor nor_1 (nor_1_out, in_1, in_1);
  LED led_1 (.in(nor_1_out));
endmodule

module _10m (
  input  in_1
);

  wire and_1_out;

  and and_1 (and_1_out, in_1, in_1);
  LED led_1 (.in(and_1_out));
endmodule

module _11m (
  input  in_1,
  input  in_2
);

  wire and_1_out;

  and and_1 (and_1_out, in_1, in_2);
  LED led_1 (.in(and_1_out));
endmodule

module _12m (
  input  in_1,
  input  in_2
);

  wire or_1_out;

  or or_1 (or_1_out, in_1, in_2);
  LED led_1 (.in(or_1_out));
endmodule

module _13m (
  input  in_1,
  input  in_2
);

  wire or_1_out;

  or or_1 (or_1_out, ~in_1, ~in_2);  // OR_Gate
  LED led_1 (.in(or_1_out));
endmodule

module _14m (
  input  in_1,
  input  in_2
);

  wire xnor_1_out;

  xnor xnor_1 (xnor_1_out, in_1, in_2);
  LED led_1 (.in(xnor_1_out));
endmodule

module _15m (
  input  in_1,
  input  in_2
);

  wire or_1_out;

  or or_1 (or_1_out, in_1, in_2);
  LED led_1 (.in(or_1_out));
endmodule

module _16m (
  input  in_1,
  input  in_2
);

  wire xnor_1_out;

  xnor xnor_1 (xnor_1_out, in_1, in_2);
  LED led_1 (.in(xnor_1_out));
endmodule

module _17m (
  input  in_1,
  input  in_2
);

  wire or_1_out;

  or or_1 (or_1_out, ~in_1, ~in_2);  // OR_Gate
  LED led_1 (.in(or_1_out));
endmodule

module _18m (
  input  in_1,
  input  in_2
);

  wire xnor_1_out;

  xnor xnor_1 (xnor_1_out, in_1, in_2);
  LED led_1 (.in(xnor_1_out));
endmodule

module _19m (
  input  in_1,
  input  in_2
);

  wire and_1_out;

  and and_1 (and_1_out, in_1, in_2);
  LED led_1 (.in(and_1_out));
endmodule

module _2H (
  input  in_1,
  input  in_2,
  input  in_3,
  input  in_4,
  output out_5,
  output out_6,
  output out_7,
  output out_8,
  output out_9,
  output out_10,
  output out_11,
  output out_12,
  output out_13,
  output out_14,
  output out_15,
  output out_16,
  output out_17,
  output out_18,
  output out_19,
  output out_20
);

  wire not_1_out, not_2_out, not_3_out, not_4_out;

  not not_1 (not_1_out, in_1);
  not not_2 (not_2_out, in_2);
  not not_3 (not_3_out, in_3);
  not not_4 (not_4_out, in_4);
  and and_1 (out_6, in_4, not_3_out, not_2_out, not_1_out);
  and and_2 (out_8, in_4, in_3, not_2_out, not_1_out);
  and and_3 (out_10, in_4, not_3_out, in_2, not_1_out);
  and and_4 (out_12, in_4, in_3, in_2, not_1_out);
  and and_5 (out_14, in_4, not_3_out, not_2_out, in_1);
  and and_6 (out_16, in_4, in_3, not_2_out, in_1);
  and and_7 (out_18, in_4, not_3_out, in_2, in_1);
  and and_8 (out_20, in_4, in_3, in_2, in_1);
  and and_9 (out_5, not_4_out, not_3_out, not_2_out, not_1_out);
  and and_10 (out_7, not_4_out, in_3, not_2_out, not_1_out);
  and and_11 (out_9, not_4_out, not_3_out, in_2, not_1_out);
  and and_12 (out_11, not_4_out, in_3, in_2, not_1_out);
  and and_13 (out_13, not_4_out, not_3_out, not_2_out, in_1);
  and and_14 (out_15, not_4_out, in_3, not_2_out, in_1);
  and and_15 (out_17, not_4_out, not_3_out, in_2, in_1);
  and and_16 (out_19, not_4_out, in_3, in_2, in_1);
endmodule
